// Logisim project KitchenSinkCPU.circ as structural Verilog
// 16ALU
module _16_bit_ALU (
  input  [15:0] A,
  input  [15:0] B,
  input  [1:0] ALU_Op,
  output [15:0] ALU_Out,
  output out_5,
  output out_6,
  output out_7
);

  wire and_1_out;
  wire [15:0] and_2_out, multiplexer_1_out, n16_bit_ripplecarry_adder_1_sum, not_1_out, or_1_out;

  Multiplexer #(.width(16), .enable("false")) multiplexer_1 (
    .in0(B), .in1(not_1_out), .out(multiplexer_1_out), .sel(and_1_out));
  assign not_1_out = ~B;  // NOT_Gate not_1, 16 bits wide
  Comparator #(.width(16)) comparator_1 (.a(A), .b(B), .gt(out_5), .eq(out_6), .lt(out_7));
  and and_1 (and_1_out, ALU_Op[0], ALU_Op[1]);
  _16_bit_ripplecarry_adder u_16_bit_ripplecarry_adder_1 (
    .C_in(and_1_out), .A(A), .B(multiplexer_1_out), .sum(n16_bit_ripplecarry_adder_1_sum));  // open: C_Out
  assign and_2_out = multiplexer_1_out & A;  // AND_Gate and_2, 16 bits wide
  assign or_1_out = multiplexer_1_out | A;  // OR_Gate or_1, 16 bits wide
  Multiplexer #(.select(2), .width(16), .enable("false")) multiplexer_2 (
    .in0(n16_bit_ripplecarry_adder_1_sum), .in1(and_2_out), .in2(or_1_out),
    .in3(n16_bit_ripplecarry_adder_1_sum), .out(ALU_Out), .sel(ALU_Op));

  // Notes on the sheet:
  //   16 Bit ALU
  //   00 = ADD
  //   01 = AND
  //   10 = OR
  //   11 = SUB
  //   sub not B
  //   sub cin
  //   sub
endmodule

// 16x16 reg
module _16x16_bit_Register_File (
  input  [15:0] Data_In,
  input  [3:0] Read_Addr_1,
  input  Write_Enable,
  input  [3:0] Write_Addr,
  input  [3:0] Read_Addr_2,
  input  Clock,
  output [15:0] Read_1_Data,
  output [15:0] Read_2_Data
);

  wire demultiplexer_1_out1, demultiplexer_1_out2, demultiplexer_1_out3, demultiplexer_1_out4,
       demultiplexer_1_out5, demultiplexer_1_out6, demultiplexer_1_out7, demultiplexer_1_out8,
       demultiplexer_1_out9, demultiplexer_1_out10, demultiplexer_1_out11, demultiplexer_1_out12,
       demultiplexer_1_out13, demultiplexer_1_out14, demultiplexer_1_out15;
  wire [15:0] register_1_q, register_2_q, register_3_q, register_4_q, register_5_q, register_6_q,
       register_7_q, register_8_q, register_9_q, register_10_q, register_11_q, register_12_q, register_13_q,
       register_14_q, register_15_q, register_16_q;

  Demultiplexer #(.select(4), .enable("false")) demultiplexer_1 (
    .out1(demultiplexer_1_out1), .out2(demultiplexer_1_out2), .out3(demultiplexer_1_out3),
    .out4(demultiplexer_1_out4), .out5(demultiplexer_1_out5), .out6(demultiplexer_1_out6),
    .out7(demultiplexer_1_out7), .out8(demultiplexer_1_out8), .out9(demultiplexer_1_out9),
    .out10(demultiplexer_1_out10), .out11(demultiplexer_1_out11), .out12(demultiplexer_1_out12),
    .out13(demultiplexer_1_out13), .out14(demultiplexer_1_out14), .out15(demultiplexer_1_out15),
    .in(Write_Enable), .sel(Write_Addr));  // open: out0
  Register #(.width(16)) register_1 (.D(Data_In), .en(1'b0), .Q(register_1_q), .clk(Clock));  // open: clr
  Register #(.width(16)) register_2 (
    .D(Data_In), .en(demultiplexer_1_out1), .Q(register_2_q), .clk(Clock));  // open: clr
  Register #(.width(16)) register_3 (
    .D(Data_In), .en(demultiplexer_1_out2), .Q(register_3_q), .clk(Clock));  // open: clr
  Register #(.width(16)) register_4 (
    .D(Data_In), .en(demultiplexer_1_out3), .Q(register_4_q), .clk(Clock));  // open: clr
  Register #(.width(16)) register_5 (
    .D(Data_In), .en(demultiplexer_1_out4), .Q(register_5_q), .clk(Clock));  // open: clr
  Register #(.width(16)) register_6 (
    .D(Data_In), .en(demultiplexer_1_out5), .Q(register_6_q), .clk(Clock));  // open: clr
  Register #(.width(16)) register_7 (
    .D(Data_In), .en(demultiplexer_1_out6), .Q(register_7_q), .clk(Clock));  // open: clr
  Register #(.width(16)) register_8 (
    .D(Data_In), .en(demultiplexer_1_out7), .Q(register_8_q), .clk(Clock));  // open: clr
  Register #(.width(16)) register_9 (
    .D(Data_In), .en(demultiplexer_1_out8), .Q(register_9_q), .clk(Clock));  // open: clr
  Register #(.width(16)) register_10 (
    .D(Data_In), .en(demultiplexer_1_out9), .Q(register_10_q), .clk(Clock));  // open: clr
  Register #(.width(16)) register_11 (
    .D(Data_In), .en(demultiplexer_1_out10), .Q(register_11_q), .clk(Clock));  // open: clr
  Register #(.width(16)) register_12 (
    .D(Data_In), .en(demultiplexer_1_out11), .Q(register_12_q), .clk(Clock));  // open: clr
  Register #(.width(16)) register_13 (
    .D(Data_In), .en(demultiplexer_1_out12), .Q(register_13_q), .clk(Clock));  // open: clr
  Register #(.width(16)) register_14 (
    .D(Data_In), .en(demultiplexer_1_out13), .Q(register_14_q), .clk(Clock));  // open: clr
  Register #(.width(16)) register_15 (
    .D(Data_In), .en(demultiplexer_1_out14), .Q(register_15_q), .clk(Clock));  // open: clr
  Register #(.width(16)) register_16 (
    .D(Data_In), .en(demultiplexer_1_out15), .Q(register_16_q), .clk(Clock));  // open: clr
  Multiplexer #(.select(4), .width(16), .enable("false")) multiplexer_1 (
    .in0(register_1_q), .in1(register_2_q), .in2(register_3_q), .in3(register_4_q), .in4(register_5_q),
    .in5(register_6_q), .in6(register_7_q), .in7(register_8_q), .in8(register_9_q), .in9(register_10_q),
    .in10(register_11_q), .in11(register_12_q), .in12(register_13_q), .in13(register_14_q),
    .in14(register_15_q), .in15(register_16_q), .out(Read_1_Data), .sel(Read_Addr_1));
  Multiplexer #(.select(4), .width(16), .enable("false")) multiplexer_2 (
    .in0(register_1_q), .in1(register_2_q), .in2(register_3_q), .in3(register_4_q), .in4(register_5_q),
    .in5(register_6_q), .in6(register_7_q), .in7(register_8_q), .in8(register_9_q), .in9(register_10_q),
    .in10(register_11_q), .in11(register_12_q), .in12(register_13_q), .in13(register_14_q),
    .in14(register_15_q), .in15(register_16_q), .out(Read_2_Data), .sel(Read_Addr_2));

  // Notes on the sheet:
  //   8x4-bit Register File
endmodule

module Control_Logic (
  input  [7:0] Op_Code,
  output Immediate,
  output Jump,
  output BNE,
  output BEQ,
  output BLT,
  output Register_File_Select,
  output Load_Word,
  output Store_Words,
  output Read_Addr_2_Select,
  output [1:0] ALU_OP,
  output Write_Enable
);

  wire not_1_out, not_2_out, not_3_out, not_4_out, not_5_out, not_6_out;

  not not_1 (not_1_out, Op_Code[4]);
  and and_1 (BNE, not_1_out, Op_Code[5]);
  and and_2 (BEQ, Op_Code[5], Op_Code[4]);
  and and_3 (BLT, Op_Code[4], not_2_out);
  not not_2 (not_2_out, Op_Code[5]);
  or or_1 (Read_Addr_2_Select, Op_Code[2], Op_Code[4], Op_Code[5]);
  not not_3 (not_3_out, Op_Code[2]);
  and and_4 (Write_Enable, not_3_out, not_4_out, not_5_out, not_6_out);
  not not_4 (not_4_out, Op_Code[5]);
  not not_5 (not_5_out, Op_Code[4]);
  not not_6 (not_6_out, Op_Code[6]);

  assign ALU_OP = Op_Code[1:0];
  assign Immediate = Op_Code[7];
  assign Jump = Op_Code[6];
  assign Load_Word = Op_Code[3];
  assign Register_File_Select = Op_Code[3];
  assign Store_Words = Op_Code[2];
endmodule

module PROCESSOR (
  output [15:0] CPU_Op_Out
);

  wire and_1_out, and_2_out, and_3_out, clock_out, control_logic_1_beq, control_logic_1_blt,
       control_logic_1_bne, control_logic_1_immediate, control_logic_1_jump, control_logic_1_load_word,
       control_logic_1_read_addr_2_select, control_logic_1_register_file_select, control_logic_1_store_words,
       control_logic_1_write_enable, n16_bit_alu_1_out_5, n16_bit_alu_1_out_6, not_1_out, or_1_out;
  wire [1:0] control_logic_1_alu_op;
  wire [3:0] multiplexer_3_out, ram_1_data;
  wire [11:0] adder_1_out, adder_2_out, bit_extender_1_out, multiplexer_1_out, multiplexer_2_out,
       register_1_q;
  wire [15:0] bit_extender_2_out, multiplexer_4_out, multiplexer_5_out,
       n16x16_bit_register_file_1_read_1_data, n16x16_bit_register_file_1_read_2_data, ram_2_data;
  wire [19:4] ram_1_data_2;

  Register #(.width(12)) register_1 (.D(multiplexer_1_out), .en(1'b1), .Q(register_1_q), .clk(clock_out));  // open: clr
  Multiplexer #(.width(12), .enable("false")) multiplexer_1 (
    .in0(multiplexer_2_out), .in1({ram_1_data_2[11:4], ram_1_data}), .out(multiplexer_1_out),
    .sel(control_logic_1_jump));
  Multiplexer #(.width(12), .enable("false")) multiplexer_2 (
    .in0(adder_2_out), .in1(adder_1_out), .out(multiplexer_2_out), .sel(or_1_out));
  and and_1 (and_1_out, n16_bit_alu_1_out_6, control_logic_1_beq);
  or or_1 (or_1_out, and_1_out, and_2_out, and_3_out);
  and and_2 (and_2_out, control_logic_1_blt, n16_bit_alu_1_out_5);
  and and_3 (and_3_out, control_logic_1_bne, not_1_out);
  Adder #(.width(12)) adder_1 (.a(bit_extender_1_out), .b(adder_2_out), .out(adder_1_out));  // open: cin, cout
  RAM #(.addrWidth(12), .dataWidth(20)) ram_1 (
    .addr(register_1_q), .data({ram_1_data_2, ram_1_data}), .sel(1'b1), .ld(1'b1));  // open: clk, clr
  Clock clock (.out(clock_out));
  Adder #(.width(12)) adder_2 (.a(register_1_q), .b(12'h1), .out(adder_2_out));  // open: cin, cout
  assign bit_extender_1_out = {{8{ram_1_data[3]}}, ram_1_data};  // Bit_Extender bit_extender_1
  not not_1 (not_1_out, n16_bit_alu_1_out_6);
  Control_Logic control_logic_1 (
    .Op_Code(ram_1_data_2[19:12]), .Immediate(control_logic_1_immediate), .Jump(control_logic_1_jump),
    .BNE(control_logic_1_bne), .BEQ(control_logic_1_beq), .BLT(control_logic_1_blt),
    .Register_File_Select(control_logic_1_register_file_select), .Load_Word(control_logic_1_load_word),
    .Store_Words(control_logic_1_store_words), .Read_Addr_2_Select(control_logic_1_read_addr_2_select),
    .ALU_OP(control_logic_1_alu_op), .Write_Enable(control_logic_1_write_enable));
  Multiplexer #(.width(4), .enable("false")) multiplexer_3 (
    .in0(ram_1_data), .in1(ram_1_data_2[11:8]), .out(multiplexer_3_out),
    .sel(control_logic_1_read_addr_2_select));
  _16x16_bit_Register_File u_16x16_bit_register_file_1 (
    .Data_In(multiplexer_4_out), .Write_Enable(control_logic_1_write_enable), .Clock(clock_out),
    .Write_Addr(ram_1_data_2[11:8]), .Read_Addr_2(multiplexer_3_out), .Read_Addr_1(ram_1_data_2[7:4]),
    .Read_1_Data(n16x16_bit_register_file_1_read_1_data), .Read_2_Data(n16x16_bit_register_file_1_read_2_data));
  assign bit_extender_2_out = {{12{ram_1_data[3]}}, ram_1_data};  // Bit_Extender bit_extender_2
  Multiplexer #(.width(16), .enable("false")) multiplexer_4 (
    .in0(CPU_Op_Out), .in1(ram_2_data), .out(multiplexer_4_out), .sel(control_logic_1_register_file_select));
  Multiplexer #(.width(16), .enable("false")) multiplexer_5 (
    .in0(n16x16_bit_register_file_1_read_2_data), .in1(bit_extender_2_out), .out(multiplexer_5_out),
    .sel(control_logic_1_immediate));
  _16_bit_ALU u_16_bit_alu_1 (
    .A(n16x16_bit_register_file_1_read_1_data), .B(multiplexer_5_out), .ALU_Op(control_logic_1_alu_op),
    .ALU_Out(CPU_Op_Out), .out_5(n16_bit_alu_1_out_5), .out_6(n16_bit_alu_1_out_6));  // open: out_7
  RAM #(.addrWidth(16), .dataWidth(16), .bus("separate")) ram_2 (
    .addr(CPU_Op_Out), .din(n16x16_bit_register_file_1_read_2_data), .data(ram_2_data),
    .str(control_logic_1_store_words), .sel(1'b1), .clk(clock_out), .ld(control_logic_1_load_word));  // open: clr

  // Notes on the sheet:
  //   PC
  //   jump
  //   instruction memory
  //   j addr
  //   Branch
  //   jump select
  //   branch offset
  //   op
  //   =
  //   BEQ
  //   BLT
  //   >
  //   BNE
  //   !=
  //   src2
  //   read selec
  //   src1
  //   dest
  //   immed data
  //   WE
  //   store select
  //   load selec
  //   reg selec
  //   immed select
  //   ALU op
  //   data memory
endmodule

// 16-adder
module _16_bit_ripplecarry_adder (
  input  C_in,
  input  [15:0] A,
  input  [15:0] B,
  output [15:0] sum,
  output C_Out
);

  wire _0_c_out, _1_c_out, _2_c_out, _3_c_out, _4_c_out, _5_c_out, _6_c_out, _7_c_out, _8_c_out, _9_c_out,
       _10_c_out, _11_c_out, _12_c_out, _13_c_out, _14_c_out;

  Full_Adder _0 (.A(A[0]), .B(B[0]), .Cin(C_in), .Sum(sum[0]), .C_out(_0_c_out));
  Full_Adder _1 (.A(A[1]), .B(B[1]), .Cin(_0_c_out), .Sum(sum[1]), .C_out(_1_c_out));
  Full_Adder _2 (.A(A[2]), .B(B[2]), .Cin(_1_c_out), .Sum(sum[2]), .C_out(_2_c_out));
  Full_Adder _3 (.A(A[3]), .B(B[3]), .Cin(_2_c_out), .Sum(sum[3]), .C_out(_3_c_out));
  Full_Adder _4 (.A(A[4]), .B(B[4]), .Cin(_3_c_out), .Sum(sum[4]), .C_out(_4_c_out));
  Full_Adder _5 (.A(A[5]), .B(B[5]), .Cin(_4_c_out), .Sum(sum[5]), .C_out(_5_c_out));
  Full_Adder _6 (.A(A[6]), .B(B[6]), .Cin(_5_c_out), .Sum(sum[6]), .C_out(_6_c_out));
  Full_Adder _7 (.A(A[7]), .B(B[7]), .Cin(_6_c_out), .Sum(sum[7]), .C_out(_7_c_out));
  Full_Adder _8 (.A(A[8]), .B(B[8]), .Cin(_7_c_out), .Sum(sum[8]), .C_out(_8_c_out));
  Full_Adder _9 (.A(A[9]), .B(B[9]), .Cin(_8_c_out), .Sum(sum[9]), .C_out(_9_c_out));
  Full_Adder _10 (.A(A[10]), .B(B[10]), .Cin(_9_c_out), .Sum(sum[10]), .C_out(_10_c_out));
  Full_Adder _11 (.A(A[11]), .B(B[11]), .Cin(_10_c_out), .Sum(sum[11]), .C_out(_11_c_out));
  Full_Adder _12 (.A(A[12]), .B(B[12]), .Cin(_11_c_out), .Sum(sum[12]), .C_out(_12_c_out));
  Full_Adder _13 (.A(A[13]), .B(B[13]), .Cin(_12_c_out), .Sum(sum[13]), .C_out(_13_c_out));
  Full_Adder _14 (.A(A[14]), .B(B[14]), .Cin(_13_c_out), .Sum(sum[14]), .C_out(_14_c_out));
  Full_Adder _15 (.A(A[15]), .B(B[15]), .Cin(_14_c_out), .Sum(sum[15]), .C_out(C_Out));
endmodule

module Half_Adder (
  input  A,
  input  B,
  output Sum,
  output C_out
);

  XOR xor_1 (.x(A), .y(B), .x_XOR_y(Sum));
  and and_1 (C_out, A, B);
endmodule

module XOR (
  input  x,
  input  y,
  output x_XOR_y
);

  wire and_1_out, and_2_out, not_1_out, not_2_out;

  not not_1 (not_1_out, x);
  not not_2 (not_2_out, y);
  and and_1 (and_1_out, not_1_out, y);
  and and_2 (and_2_out, x, not_2_out);
  or or_1 (x_XOR_y, and_1_out, and_2_out);
endmodule

// FA
module Full_Adder (
  input  A,
  input  B,
  input  Cin,
  output Sum,
  output C_out
);

  wire half_adder_1_c_out, half_adder_1_sum, half_adder_2_c_out;

  Half_Adder half_adder_1 (.A(A), .B(B), .Sum(half_adder_1_sum), .C_out(half_adder_1_c_out));
  Half_Adder half_adder_2 (.A(half_adder_1_sum), .B(Cin), .Sum(Sum), .C_out(half_adder_2_c_out));
  or or_1 (C_out, half_adder_2_c_out, half_adder_1_c_out);
endmodule
